# Fritzing sketch weather_station (saved by Fritzing 0.9.3b)
breadboards: 1

parts:
  Composant1 = Arduino Nano (Rev3.0)
  Composant3 = Adafruit BME280
  Nokia_5110_LCD_Module2 = Nokia5110LCDModule
  S1 = Momentary Switch [package=ksa_sealed_tac_switch]
  S2 = Momentary Switch [package=ksa_sealed_tac_switch]

nets:
  GND: Composant1.GND, Composant3.GND, Nokia_5110_LCD_Module2.SCLK, Nokia_5110_LCD_Module2.LED, S1.3, S2.3
  N1: Composant1.D3, Nokia_5110_LCD_Module2.D/C
  N2: Composant1.D4, Nokia_5110_LCD_Module2.RST
  N3: Composant1.D5, Nokia_5110_LCD_Module2.SCE
  N4: Composant1.D6, Nokia_5110_LCD_Module2.Grnd
  N5: Composant1.D7, Nokia_5110_LCD_Module2.Vcc
  VIN: Composant1.VIN, Composant3.VIN
  N6: Composant1.5V, Nokia_5110_LCD_Module2.6_DN_(MOSI)
  N7: Composant1.A5, Composant3.SCK/SCL
  N8: Composant1.A4, Composant3.SDI/SDA
  N9: Composant1.A1, S1.4
  N10: Composant1.A0, S2.4

notes:
  https://www.sla99.fr

custom parts:
  Adafruit BME280: Bosch has stepped up their game with their new BME280 sensor, an environmental sensor with temperature, barometric pressure and humidity! This sensor is great for all sorts of weather/environmental sensing and can even be used in both I2C and SPI! This precision sensor from Bosch is the best low-cost sensing solution for measuring humidity with ±3% accuracy, barometric pressure with ±1 hPa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
  : Nokia 5110 LCD with 8 pin. It's a 45mm*45mm module part. Description: The Nokia 5110 is a basic graphic LCD screen for lots of applications. It was originally intended for as a cell phone screen. This one is mounted on an easy to solder PCB. It uses the PCD8544 controller. The PCD8544 is a low power CMOS LCD controller/driver, designed to drive a graphic display of 48 rows and 84 columns. All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
